// Logisim project cdm16_verilog.circ as structural Verilog: 5 circuits, main circuit cdm16
module cdm16 (
  input  [15:0] data_in,
  input  EXC,
  input  [5:0] exc_vec,
  input  IRQ,
  input  [5:0] int_vec,
  input  clock,
  input  hold,
  output mem,
  output data_ins_prime,
  output rd_wr_prime,
  output word,
  output [15:0] address,
  output [15:0] SP,
  output [15:0] PC,
  output [15:0] data_out,
  output [15:0] PS,
  output fetch,
  output IAck,
  output [15:0] R0,
  output [15:0] R1,
  output [15:0] R2,
  output [15:0] R3,
  output [15:0] R4,
  output [15:0] R5,
  output [15:0] R6,
  output [15:0] FP,
  output [1:0] status
);

  wire clk, clk_no_inhibit, int_en;

  // verilator_component_1_0_SNAPSHOT_all_cdm16 cdm16_1: pin names not known; wires that end beside it: R0, R1, R2, R3, R4, R5, R6, FP, fetch, clock, hold, IRQ, SP, PC, PS, address, mem, data_ins_prime, rd_wr_prime, word, data_out, data_in, int_en
  LED led_1 (.in(int_en));
  LED led_2 (.in(clk));
  LED led_3 (.in(clk_no_inhibit));

  // Other names for the same wires on the sheet: data = data_ins_prime; dbg_input_clock = clock;
  //   dbg_input_hold = hold; direct_exc_vec[5:0] = exc_vec; exc_trig_ext = EXC; pc_value[15:0] = PC;
  //   ps_value[15:0] = PS; read = rd_wr_prime; sp_value[15:0] = SP

  // Notes on the sheet:
  //   hold: pull=down
  //   EXC: pull=down
  //   clock: pull=down
  //   IRQ: pull=down
  //   data_in: pull=down
  //   1 - waiting
  //   2 - halted
  //   3 - fault
  //   0 - running
endmodule

module sp_register (
  input  [15:0] In,
  input  clr,
  input  clk,
  input  plus_2,
  input  en,
  input  minus_2,
  output [15:0] Out,
  output [15:0] Mon
);

  wire count, en_t;
  wire [15:0] incdec2_1_out, multiplexer_1_out;

  Multiplexer #(.width(16), .disabled(0), .enable("false")) multiplexer_1 (
    .in0(In), .in1(incdec2_1_out), .out(multiplexer_1_out), .sel(count));
  Register #(.width(16), .trigger("falling")) register_1 (
    .D(multiplexer_1_out), .en(en_t), .Q(Mon), .clk(clk), .clr(clr));
  or or_1 (count, plus_2, minus_2);
  or or_2 (en_t, count, en);
  incdec2 incdec2_1 (.in(Mon), .out(incdec2_1_out), .inc_dec_prime(plus_2));
  Multiplexer #(.width(16), .disabled(0), .enable("false")) multiplexer_2 (
    .in0(Mon), .in1(incdec2_1_out), .out(Out), .sel(minus_2));

  // Notes on the sheet:
  //   clk: pull=down
  //   minus_2: pull=down
  //   clr: pull=down
  //   en: pull=up
  //   plus_2: pull=down
endmodule

module pc_register (
  input  [15:0] In,
  input  clr,
  input  clk,
  input  en,
  input  plus_2,
  input  asrt_inc,
  input  inverse_inc,
  output [15:0] Out,
  output [15:0] Mon
);

  wire en_t, not_1_out;
  wire [15:0] incdec2_1_out, multiplexer_1_out;

  Multiplexer #(.width(16), .disabled(0), .enable("false")) multiplexer_1 (
    .in0(In), .in1(incdec2_1_out), .out(multiplexer_1_out), .sel(plus_2));
  Register #(.width(16), .trigger("falling")) register_1 (
    .D(multiplexer_1_out), .en(en_t), .Q(Mon), .clk(clk), .clr(clr));
  or or_1 (en_t, plus_2, en);
  incdec2 incdec2_1 (.in(Mon), .out(incdec2_1_out), .inc_dec_prime(not_1_out));
  not not_1 (not_1_out, inverse_inc);
  Multiplexer #(.width(16), .disabled(0), .enable("false")) multiplexer_2 (
    .in0(Mon), .in1(incdec2_1_out), .out(Out), .sel(asrt_inc));

  // Other names for the same wires on the sheet: count = plus_2

  // Notes on the sheet:
  //   plus_2: pull=down
  //   en: pull=up
  //   clr: pull=down
  //   clk: pull=down
  //   asrt_inc: pull=down
  //   inverse_inc: pull=down
endmodule

module ps_register (
  input  [3:0] flags,
  input  [15:0] word,
  input  clk,
  input  latch_word,
  input  latch_flags,
  input  ei,
  input  di,
  output [3:0] out_flags,
  output [15:0] out
);

  wire or_1_out, or_3_out, set_int_flag;
  wire [15:0] multiplexer_1_out, multiplexer_2_out;

  Multiplexer #(.width(16), .enable("false")) multiplexer_1 (
    .in0({out[15:4], flags}), .in1({ei, out[14:0]}), .out(multiplexer_1_out), .sel(set_int_flag));
  Multiplexer #(.width(16), .enable("false")) multiplexer_2 (
    .in0(multiplexer_1_out), .in1(word), .out(multiplexer_2_out), .sel(latch_word));
  or or_1 (or_1_out, latch_word, latch_flags);
  or or_2 (set_int_flag, ei, di);
  Register #(.width(16), .trigger("falling")) register_1 (
    .D(multiplexer_2_out), .en(or_3_out), .Q(out), .clk(clk));  // open: clr
  or or_3 (or_3_out, or_1_out, set_int_flag);
  Bit_Extender #(.in_width(16), .out_width(4)) bit_extender_1 (.in(out), .out(out_flags));

  // Notes on the sheet:
  //   latch_word: pull=down
  //   di: pull=down
  //   ei: pull=down
  //   flags: pull=down
  //   word: pull=down
  //   clk: pull=down
  //   latch_flags: pull=down
endmodule

module incdec2 (
  input  [15:0] in,
  input  inc_dec_prime,
  output [15:0] out
);

  wire [15:0] multiplexer_1_out;

  Multiplexer #(.width(16), .enable("false")) multiplexer_1 (
    .in0(16'hfffe), .in1(16'h2), .out(multiplexer_1_out), .sel(inc_dec_prime));
  Adder #(.width(16)) adder_1 (.a(in), .b(multiplexer_1_out), .out(out));  // open: cin, cout

  // Notes on the sheet:
  //   inc_dec_prime: pull=up
endmodule
